# Fritzing sketch Fritzing_Projet_Arroseur_Sylvain_Alex (saved by Fritzing 0.9.10b)
breadboards: 1

parts:
  Composant1 = Arduino Uno (Rev3)
  Composant2 = Soil Moisture Sensor
  WATER_PUMP1 = water pump/motor
  U1 = RELAY [package=relay-jzc]
  Composant3 = Ambient Light Sensor (TEMT6000 Breakout Board)
  J1 = Power Jack [package=power_jack_slot]

nets (from the breadboard view):
  N1: Composant1.A0, Composant3.S
  N2: Composant1.A1, Composant2.SIG
  N3: Composant1.D4, U1.NO
  VCC: Composant1.5V, Composant2.VCC, U1.COIL2, Composant3.VCC
  GND: Composant1.GND, Composant2.GND, WATER_PUMP1.pin_1, U1.NC, Composant3.GND, J1.GND
  N4: WATER_PUMP1.pin_2, U1.MAIN
  N5: U1.COIL1, J1.GNDBREAK

notes:
  Relais:
  IN: Signal Digital Arduino
  DC+: 5VDC
  DC-: GND
  NO: Sortie de la pompe
  COM: 12VDC
  230VAC / 12VDC Adaptateur
  Pompe 5-12VDC
  Capteur d'humidité
  Capteur de lumière (LDR)

custom parts:
  water pump/motor: WATER PUMP BY ARDUBLOCKTR
